# Fritzing sketch SmartBridge (saved by Fritzing 1.0.3b)
breadboards: 3

parts:
  Part1 = Arduino Uno (Rev3)
  Part2 = Soil Moisture Sensor
  J1 = Piezo Speaker
  M1 = Dagu DGServo 9g (Pan and tilt) [part_number=RS001B]
  M2 = Dagu DGServo 9g (Pan and tilt) [part_number=RS001B]
  A1 = BBAA100043
  A2 = BBAA100043

nets:
  N1: Part1.D8, A1.pin3
  N2: Part1.D9_PWM, A1.pin2
  N3: Part1.D10_PWM/SS, A1.pin1
  N4: Part1.D11_PWM/MOSI, A2.pin3
  N5: Part1.D12/MISO, A2.pin2
  N6: Part1.D13/SCK, A2.pin1
  N7: Part1.D3_PWM, M2.pulse
  N8: Part1.D4, M1.pulse
  N9: Part1.D5_PWM, Part2.SIG
  N10: Part1.D7, J1.pin2
  VCC: Part1.5V, Part2.VCC, M1.vcc, M2.vcc
  GND: Part1.GND, Part2.GND, J1.pin1, M1.gnd, M2.gnd, A1.pin4, A2.pin4

custom parts:
  BBAA100043: BBAA100043 traffic light module.
